# Fritzing sketch clock_v3 (saved by Fritzing 0.9.3b)
circuit board: 15.2cm x 8.40001cm
breadboards: 2

parts:
  7_Segment1 = 7 Segment Display
  7_Segment2 = 7 Segment Display
  7_Segment3 = 7 Segment Display
  7_Segment4 = 7 Segment Display
  7_Segment5 = 7 Segment Display
  7_Segment6 = 7 Segment Display
  U1 = 74HC595 [package="DIP16 [THT]"]
  Part1 = Arduino Nano (Rev3.0)
  U6 = 74HC595 [package="DIP16 [THT]"]
  U5 = 74HC595 [package="DIP16 [THT]"]
  U4 = 74HC595 [package="DIP16 [THT]"]
  U3 = 74HC595 [package="DIP16 [THT]"]
  U2 = 74HC595 [package="DIP16 [THT]"]
  R53 = Resistor [tolerance=±5% resistance=220 package=THT]
  R52 = Resistor [tolerance=±5% resistance=220 package=THT]
  R12 = Resistor [tolerance=±5% resistance=220 package=THT]
  R11 = Resistor [tolerance=±5% resistance=220 package=THT]
  R13 = Resistor [tolerance=±5% resistance=220 package=THT]
  R7 = Resistor [tolerance=±5% resistance=220 package=THT]
  R10 = Resistor [tolerance=±5% resistance=220 package=THT]
  R9 = Resistor [tolerance=±5% resistance=220 package=THT]
  R14 = Resistor [tolerance=±5% resistance=220 package=THT]
  R8 = Resistor [tolerance=±5% resistance=220 package=THT]
  R30 = Resistor [tolerance=±5% resistance=220 package=THT]
  R15 = Resistor [tolerance=±5% resistance=220 package=THT]
  R25 = Resistor [tolerance=±5% resistance=220 package=THT]
  R35 = Resistor [tolerance=±5% resistance=220 package=THT]
  R40 = Resistor [tolerance=±5% resistance=220 package=THT]
  R50 = Resistor [tolerance=±5% resistance=220 package=THT]
  R45 = Resistor [tolerance=±5% resistance=220 package=THT]
  R20 = Resistor [tolerance=±5% resistance=220 package=THT]
  R46 = Resistor [tolerance=±5% resistance=220 package=THT]
  R41 = Resistor [tolerance=±5% resistance=220 package=THT]
  R16 = Resistor [tolerance=±5% resistance=220 package=THT]
  R21 = Resistor [tolerance=±5% resistance=220 package=THT]
  R36 = Resistor [tolerance=±5% resistance=220 package=THT]
  R31 = Resistor [tolerance=±5% resistance=220 package=THT]
  R26 = Resistor [tolerance=±5% resistance=220 package=THT]
  R51 = Resistor [tolerance=±5% resistance=220 package=THT]
  R49 = Resistor [tolerance=±5% resistance=220 package=THT]
  R42 = Resistor [tolerance=±5% resistance=220 package=THT]
  R17 = Resistor [tolerance=±5% resistance=220 package=THT]
  R22 = Resistor [tolerance=±5% resistance=220 package=THT]
  R37 = Resistor [tolerance=±5% resistance=220 package=THT]
  R32 = Resistor [tolerance=±5% resistance=220 package=THT]
  R27 = Resistor [tolerance=±5% resistance=220 package=THT]
  R33 = Resistor [tolerance=±5% resistance=220 package=THT]
  R47 = Resistor [tolerance=±5% resistance=220 package=THT]
  R43 = Resistor [tolerance=±5% resistance=220 package=THT]
  R18 = Resistor [tolerance=±5% resistance=220 package=THT]
  R23 = Resistor [tolerance=±5% resistance=220 package=THT]
  R38 = Resistor [tolerance=±5% resistance=220 package=THT]
  R28 = Resistor [tolerance=±5% resistance=220 package=THT]
  R48 = Resistor [tolerance=±5% resistance=220 package=THT]
  R44 = Resistor [tolerance=±5% resistance=220 package=THT]
  R19 = Resistor [tolerance=±5% resistance=220 package=THT]
  R24 = Resistor [tolerance=±5% resistance=220 package=THT]
  R39 = Resistor [tolerance=±5% resistance=220 package=THT]
  R34 = Resistor [tolerance=±5% resistance=220 package=THT]
  R29 = Resistor [tolerance=±5% resistance=220 package=THT]
  R54 = Resistor [tolerance=±5% resistance=220 package=THT]
  DS3231 = female pin header, 5 pins [form="♀ (female)"]

nets:
  N1: 7_Segment1.Segment_E, R11.Pin_1
  N2: 7_Segment1.Segment_D, R10.Pin_1
  GND: 7_Segment1.common_cathode, 7_Segment2.common_cathode, 7_Segment3.common_cathode, 7_Segment4.common_cathode, 7_Segment5.common_cathode, 7_Segment6.common_cathode, U1.GND, U1.OE, Part1.GND, U6.GND, U6.OE, U5.GND, U5.OE, U4.GND, U4.OE, U3.GND, U3.OE, U2.GND, U2.OE, DS3231.pin5
  N3: 7_Segment1.Segment_C, R9.Pin_1
  N4: 7_Segment1.Segment_DP, R14.Pin_1
  N5: 7_Segment1.Segment_B, R8.Pin_0
  N6: 7_Segment1.Segment_A, R7.Pin_0
  N7: 7_Segment1.Segment_F, R12.Pin_0
  N8: 7_Segment1.Segment_G, R13.Pin_0
  N9: 7_Segment2.Segment_E, R35.Pin_1
  N10: 7_Segment2.Segment_D, R30.Pin_1
  N11: 7_Segment2.Segment_C, R25.Pin_1
  N12: 7_Segment2.Segment_DP, R50.Pin_1
  N13: 7_Segment2.Segment_B, R20.Pin_0
  N14: 7_Segment2.Segment_A, R15.Pin_0
  N15: 7_Segment2.Segment_F, R40.Pin_0
  N16: 7_Segment2.Segment_G, R45.Pin_0
  N17: 7_Segment3.Segment_E, R36.Pin_1
  N18: 7_Segment3.Segment_D, R31.Pin_1
  N19: 7_Segment3.Segment_C, R26.Pin_1
  N20: 7_Segment3.Segment_DP, R51.Pin_1
  N21: 7_Segment3.Segment_B, R21.Pin_0
  N22: 7_Segment3.Segment_A, R16.Pin_0
  N23: 7_Segment3.Segment_F, R41.Pin_0
  N24: 7_Segment3.Segment_G, R46.Pin_0
  N25: 7_Segment4.Segment_E, R37.Pin_1
  N26: 7_Segment4.Segment_D, R32.Pin_1
  N27: 7_Segment4.Segment_C, R27.Pin_1
  N28: 7_Segment4.Segment_DP, R52.Pin_1
  N29: 7_Segment4.Segment_B, R22.Pin_0
  N30: 7_Segment4.Segment_A, R17.Pin_0
  N31: 7_Segment4.Segment_F, R42.Pin_0
  N32: 7_Segment4.Segment_G, R49.Pin_0
  N33: 7_Segment5.Segment_E, R38.Pin_1
  N34: 7_Segment5.Segment_D, R33.Pin_1
  N35: 7_Segment5.Segment_C, R28.Pin_1
  N36: 7_Segment5.Segment_DP, R53.Pin_1
  N37: 7_Segment5.Segment_B, R23.Pin_0
  N38: 7_Segment5.Segment_A, R18.Pin_0
  N39: 7_Segment5.Segment_F, R43.Pin_0
  N40: 7_Segment5.Segment_G, R47.Pin_0
  N41: 7_Segment6.Segment_E, R39.Pin_1
  N42: 7_Segment6.Segment_D, R34.Pin_1
  N43: 7_Segment6.Segment_C, R29.Pin_1
  N44: 7_Segment6.Segment_DP, R54.Pin_1
  N45: 7_Segment6.Segment_B, R24.Pin_0
  N46: 7_Segment6.Segment_A, R19.Pin_0
  N47: 7_Segment6.Segment_F, R44.Pin_0
  N48: 7_Segment6.Segment_G, R48.Pin_0
  N49: U1.Q1, R8.Pin_1
  N50: U1.Q2, R9.Pin_0
  N51: U1.Q3, R10.Pin_0
  N52: U1.Q4, R11.Pin_0
  N53: U1.Q5, R12.Pin_1
  N54: U1.Q6, R13.Pin_1
  N55: U1.Q7, R14.Pin_0
  VCC: U1.MR, U1.VCC, Part1.5V, U6.MR, U6.VCC, U5.MR, U5.VCC, U4.MR, U4.VCC, U3.MR, U3.VCC, U2.MR, U2.VCC, DS3231.pin1
  N56: U1.SH_CP, Part1.D10, U6.SH_CP, U5.SH_CP, U4.SH_CP, U3.SH_CP, U2.SH_CP
  N57: U1.ST_CP, Part1.D9, U6.ST_CP, U5.ST_CP, U4.ST_CP, U3.ST_CP, U2.ST_CP
  N58: U1.DS, U2.Q7'
  N59: U1.Q0, R7.Pin_1
  N60: Part1.D8, U6.DS
  N61: Part1.A5, DS3231.pin3
  N62: Part1.A4, DS3231.pin2
  N63: U6.Q1, R24.Pin_1
  N64: U6.Q2, R29.Pin_0
  N65: U6.Q3, R34.Pin_0
  N66: U6.Q4, R39.Pin_0
  N67: U6.Q5, R44.Pin_1
  N68: U6.Q6, R48.Pin_1
  N69: U6.Q7, R54.Pin_0
  N70: U6.Q7', U5.DS
  N71: U6.Q0, R19.Pin_1
  N72: U5.Q1, R23.Pin_1
  N73: U5.Q2, R28.Pin_0
  N74: U5.Q3, R33.Pin_0
  N75: U5.Q4, R38.Pin_0
  N76: U5.Q5, R43.Pin_1
  N77: U5.Q6, R47.Pin_1
  N78: U5.Q7, R53.Pin_0
  N79: U5.Q7', U4.DS
  N80: U5.Q0, R18.Pin_1
  N81: U4.Q1, R22.Pin_1
  N82: U4.Q2, R27.Pin_0
  N83: U4.Q3, R32.Pin_0
  N84: U4.Q4, R37.Pin_0
  N85: U4.Q5, R42.Pin_1
  N86: U4.Q6, R49.Pin_1
  N87: U4.Q7, R52.Pin_0
  N88: U4.Q7', U3.DS
  N89: U4.Q0, R17.Pin_1
  N90: U3.Q1, R21.Pin_1
  N91: U3.Q2, R26.Pin_0
  N92: U3.Q3, R31.Pin_0
  N93: U3.Q4, R36.Pin_0
  N94: U3.Q5, R41.Pin_1
  N95: U3.Q6, R46.Pin_1
  N96: U3.Q7, R51.Pin_0
  N97: U3.Q7', U2.DS
  N98: U3.Q0, R16.Pin_1
  N99: U2.Q1, R20.Pin_1
  N100: U2.Q2, R25.Pin_0
  N101: U2.Q3, R30.Pin_0
  N102: U2.Q4, R35.Pin_0
  N103: U2.Q5, R40.Pin_1
  N104: U2.Q6, R45.Pin_1
  N105: U2.Q7, R50.Pin_0
  N106: U2.Q0, R15.Pin_1

notes:
  7-Segment Clock
  By Zachary Rubin
